// Logisim project 8251A.circ as structural Verilog: 3 circuits, main circuit PtoS
module PtoS (
  input  [7:0] D,
  input  CLK,
  input  SI,
  input  SHIFT_LOAD,
  output SO
);

  wire d_ff_1_q, d_ff_2_q, d_ff_3_q, d_ff_4_q, d_ff_5_q, d_ff_6_q, d_ff_7_q, multiplexer_1_out,
       multiplexer_2_out, multiplexer_3_out, multiplexer_4_out, multiplexer_5_out, multiplexer_6_out,
       multiplexer_7_out, multiplexer_8_out;

  Multiplexer multiplexer_1 (.in0(D[0]), .in1(SI), .out(multiplexer_1_out), .sel(SHIFT_LOAD));  // open: en
  D_Flip_Flop d_ff_1 (.clk(CLK), .D(multiplexer_1_out), .Q(d_ff_1_q));  // open: Qn, preset, en, reset
  Multiplexer multiplexer_2 (.in0(D[1]), .in1(d_ff_1_q), .out(multiplexer_2_out), .sel(SHIFT_LOAD));  // open: en
  D_Flip_Flop d_ff_2 (.clk(CLK), .D(multiplexer_2_out), .Q(d_ff_2_q));  // open: Qn, preset, en, reset
  Multiplexer multiplexer_3 (.in0(D[2]), .in1(d_ff_2_q), .out(multiplexer_3_out), .sel(SHIFT_LOAD));  // open: en
  D_Flip_Flop d_ff_3 (.clk(CLK), .D(multiplexer_3_out), .Q(d_ff_3_q));  // open: Qn, preset, en, reset
  Multiplexer multiplexer_4 (.in0(D[3]), .in1(d_ff_3_q), .out(multiplexer_4_out), .sel(SHIFT_LOAD));  // open: en
  D_Flip_Flop d_ff_4 (.clk(CLK), .D(multiplexer_4_out), .Q(d_ff_4_q));  // open: Qn, preset, en, reset
  Multiplexer multiplexer_5 (.in0(D[4]), .in1(d_ff_4_q), .out(multiplexer_5_out), .sel(SHIFT_LOAD));  // open: en
  D_Flip_Flop d_ff_5 (.clk(CLK), .D(multiplexer_5_out), .Q(d_ff_5_q));  // open: Qn, preset, en, reset
  Multiplexer multiplexer_6 (.in0(D[5]), .in1(d_ff_5_q), .out(multiplexer_6_out), .sel(SHIFT_LOAD));  // open: en
  D_Flip_Flop d_ff_6 (.clk(CLK), .D(multiplexer_6_out), .Q(d_ff_6_q));  // open: Qn, preset, en, reset
  Multiplexer multiplexer_7 (.in0(D[6]), .in1(d_ff_6_q), .out(multiplexer_7_out), .sel(SHIFT_LOAD));  // open: en
  Multiplexer multiplexer_8 (.in0(D[7]), .in1(d_ff_7_q), .out(multiplexer_8_out), .sel(SHIFT_LOAD));  // open: en
  D_Flip_Flop d_ff_7 (.clk(CLK), .D(multiplexer_7_out), .Q(d_ff_7_q));  // open: Qn, preset, en, reset
  D_Flip_Flop d_ff_8 (.clk(CLK), .D(multiplexer_8_out), .Q(SO));  // open: Qn, preset, en, reset
endmodule

module StoP (
  input  CLK,
  input  SI,
  output [7:0] D
);

  D_Flip_Flop d_ff_1 (.clk(CLK), .D(SI), .Q(D[0]));  // open: Qn, preset, en, reset
  D_Flip_Flop d_ff_2 (.clk(CLK), .D(D[0]), .Q(D[1]));  // open: Qn, preset, en, reset
  D_Flip_Flop d_ff_3 (.clk(CLK), .D(D[1]), .Q(D[2]));  // open: Qn, preset, en, reset
  D_Flip_Flop d_ff_4 (.clk(CLK), .D(D[2]), .Q(D[3]));  // open: Qn, preset, en, reset
  D_Flip_Flop d_ff_5 (.clk(CLK), .D(D[3]), .Q(D[4]));  // open: Qn, preset, en, reset
  D_Flip_Flop d_ff_6 (.clk(CLK), .D(D[4]), .Q(D[5]));  // open: Qn, preset, en, reset
  D_Flip_Flop d_ff_7 (.clk(CLK), .D(D[5]), .Q(D[6]));  // open: Qn, preset, en, reset
  D_Flip_Flop d_ff_8 (.clk(CLK), .D(D[6]), .Q(D[7]));  // open: Qn, preset, en, reset
endmodule

module \_8251А  (
  input  in_1,
  input  [7:0] D,
  input  CTS,
  input  WR,
  input  RD,
  input  RxD,
  input  CS,
  output TxD,
  output [7:0] D_2
);

  wire and_1_out, clock_1_out, d_ff_1_q, not_1_out, not_2_out, not_3_out, not_4_out;
  wire [7:0] controlled_buffer_1_out, stop_1_d;

  assign controlled_buffer_1_out = not_1_out ? D : 8'bz;  // Controlled_Buffer controlled_buffer_1
  assign D_2 = not_2_out ? stop_1_d : 8'bz;  // Controlled_Buffer controlled_buffer_2
  not not_1 (not_1_out, WR);
  not not_2 (not_2_out, RD);
  D_Flip_Flop d_ff_1 (.clk(and_1_out), .D(not_3_out), .Q(d_ff_1_q));  // open: Qn, preset, en, reset
  not not_3 (not_3_out, CTS);
  PtoS ptos_1 (.SI(in_1), .SHIFT_LOAD(d_ff_1_q), .CLK(and_1_out), .SO(TxD), .D(controlled_buffer_1_out));
  StoP stop_1 (.SI(RxD), .CLK(and_1_out), .D(stop_1_d));
  and and_1 (and_1_out, not_4_out, clock_1_out);
  not not_4 (not_4_out, CS);
  Clock clock_1 (.out(clock_1_out));
endmodule
