// Logisim project 8255.circ as structural Verilog: 1 circuit, main circuit main
module main (
  input  [7:0] addr,
  input  [7:0] in_2,
  input  [7:0] in_3,
  input  [7:0] in_4,
  input  [7:0] data,
  input  WR,
  input  RD,
  input  reset,
  output [7:0] out_9,
  output [7:0] out_10,
  output [15:0] out_11
);

  wire clock_1_out, CS_out, decoder_1_out0, decoder_1_out1, decoder_1_out2, decoder_1_out3, decoder_2_out0,
       decoder_2_out1, decoder_2_out2, decoder_2_out3, decoder_2_out4, decoder_2_out5, decoder_2_out6,
       decoder_2_out7, not_1_out, not_2_out;
  wire [7:0] controlled_buffer_1_out, controlled_buffer_3_out, controlled_buffer_5_out, register_2_q,
       register_4_q, register_7_q;
  wire [15:0] controlled_buffer_4_out;

  assign controlled_buffer_1_out = WR ? data : 8'bz;  // Controlled_Buffer controlled_buffer_1
  assign out_11 = RD ? controlled_buffer_4_out : 16'bz;  // Controlled_Buffer controlled_buffer_2
  assign controlled_buffer_3_out = not_1_out ? controlled_buffer_1_out : 8'bz;  // Controlled_Buffer controlled_buffer_3
  not not_1 (not_1_out, register_7_q[4]);
  assign controlled_buffer_4_out[7:0] = register_7_q[4] ? register_2_q : 8'bz;  // Controlled_Buffer controlled_buffer_4
  not not_2 (not_2_out, register_7_q[1]);
  and CS (CS_out, addr[2], addr[3], addr[4], addr[5], addr[6], addr[7]);
  assign controlled_buffer_5_out = not_2_out ? controlled_buffer_1_out : 8'bz;  // Controlled_Buffer controlled_buffer_5
  assign controlled_buffer_4_out[15:8] = register_7_q[1] ? register_4_q : 8'bz;  // Controlled_Buffer controlled_buffer_6
  Clock clock_1 (.out(clock_1_out));
  Decoder #(.select(2)) decoder_1 (
    .out0(decoder_1_out0), .out1(decoder_1_out1), .out2(decoder_1_out2), .out3(decoder_1_out3),
    .sel(addr[1:0]), .en(CS_out));
  Register register_1 (.D(controlled_buffer_3_out), .en(decoder_1_out0), .Q(out_9), .clk(clock_1_out), .clr(reset));
  Register register_2 (.D(in_2), .en(decoder_1_out0), .Q(register_2_q), .clk(clock_1_out), .clr(reset));
  Register register_3 (.D(controlled_buffer_5_out), .en(decoder_1_out1), .Q(out_10), .clk(clock_1_out), .clr(reset));
  Register register_4 (.D(in_4), .en(decoder_1_out1), .Q(register_4_q), .clk(clock_1_out), .clr(reset));
  Register register_5 (.en(decoder_1_out2), .clk(clock_1_out), .clr(reset));  // open: D, Q
  Register register_6 (.en(decoder_1_out2), .clk(clock_1_out), .clr(reset));  // open: D, Q
  Register register_7 (
    .D(controlled_buffer_1_out), .en(decoder_1_out3), .Q(register_7_q), .clk(clock_1_out), .clr(reset));
  Register register_8 (.en(decoder_1_out3), .clk(clock_1_out), .clr(reset));  // open: D, Q
  Decoder #(.select(3)) decoder_2 (
    .out0(decoder_2_out0), .out1(decoder_2_out1), .out2(decoder_2_out2), .out3(decoder_2_out3),
    .out4(decoder_2_out4), .out5(decoder_2_out5), .out6(decoder_2_out6), .out7(decoder_2_out7),
    .sel(register_7_q[3:1]), .en(CS_out));
  D_Flip_Flop d_ff_1 (
    .clk(clock_1_out), .D(register_7_q[0]), .Q(in_3[0]), .en(decoder_2_out0), .reset(reset));  // open: Qn, preset
  D_Flip_Flop d_ff_2 (
    .clk(clock_1_out), .D(register_7_q[0]), .Q(in_3[1]), .en(decoder_2_out1), .reset(reset));  // open: Qn, preset
  D_Flip_Flop d_ff_3 (
    .clk(clock_1_out), .D(register_7_q[0]), .Q(in_3[2]), .en(decoder_2_out2), .reset(reset));  // open: Qn, preset
  D_Flip_Flop d_ff_4 (
    .clk(clock_1_out), .D(register_7_q[0]), .Q(in_3[3]), .en(decoder_2_out3), .reset(reset));  // open: Qn, preset
  D_Flip_Flop d_ff_5 (
    .clk(clock_1_out), .D(register_7_q[0]), .Q(in_3[4]), .en(decoder_2_out4), .reset(reset));  // open: Qn, preset
  D_Flip_Flop d_ff_6 (
    .clk(clock_1_out), .D(register_7_q[0]), .Q(in_3[5]), .en(decoder_2_out5), .reset(reset));  // open: Qn, preset
  D_Flip_Flop d_ff_7 (
    .clk(clock_1_out), .D(register_7_q[0]), .Q(in_3[6]), .en(decoder_2_out6), .reset(reset));  // open: Qn, preset
  D_Flip_Flop d_ff_8 (
    .clk(clock_1_out), .D(register_7_q[0]), .Q(in_3[7]), .en(decoder_2_out7), .reset(reset));  // open: Qn, preset
endmodule
