// Logisim project 8255A.circ as structural Verilog: 4 circuits, main circuit main
module main (
  input  [7:0] D0_D7,
  input  not_WR,
  input  not_RD,
  input  not_CS,
  input  [1:0] A01,
  input  RESET,
  output [7:0] Pa0_Pa7,
  output [7:0] \Упр_слово ,
  output [7:0] out_9,
  output [7:0] Pc0_Pc7,
  output [7:0] Pb0_Pb7
);

  wire clock_1_out, decoder_1_out0, decoder_1_out1, decoder_1_out2, decoder_1_out3, not_1_out;
  wire [3:0] controlled_buffer_1_out, controlled_buffer_1_out_2;
  wire [7:0] controlled_buffer_3_out, PA_pa_out_wr, PB_pb_out_wr, PC_pc0_pc3_out_wr;

  Decoder #(.select(2)) decoder_1 (
    .out0(decoder_1_out0), .out1(decoder_1_out1), .out2(decoder_1_out2), .out3(decoder_1_out3), .sel(A01),
    .en(not_1_out));
  not not_1 (not_1_out, not_CS);
  assign {controlled_buffer_1_out_2, controlled_buffer_1_out} = not_WR ? D0_D7 : 8'bz;  // Controlled_Buffer controlled_buffer_1
  assign out_9 = not_RD ? controlled_buffer_3_out : 8'bz;  // Controlled_Buffer controlled_buffer_2
  assign controlled_buffer_3_out = decoder_1_out0 ? PA_pa_out_wr : 8'bz;  // Controlled_Buffer controlled_buffer_3
  assign controlled_buffer_3_out = decoder_1_out2 ? PC_pc0_pc3_out_wr : 8'bz;  // Controlled_Buffer controlled_buffer_4
  assign controlled_buffer_3_out = decoder_1_out1 ? PB_pb_out_wr : 8'bz;  // Controlled_Buffer controlled_buffer_5
  Register CR (
    .D({controlled_buffer_1_out_2, controlled_buffer_1_out}), .en(decoder_1_out3), .Q(\Упр_слово ),
    .clk(clock_1_out), .clr(RESET));
  Clock clock_1 (.out(clock_1_out));
  port_A PA (
    .D0_D7(\Упр_слово ), .PA_in_WR(Pa0_Pa7), .PA_out_RD(Pa0_Pa7), .Enable(decoder_1_out0), .RESET(RESET),
    .CLK(clock_1_out), .PA_out_WR(PA_pa_out_wr),
    .PA_in_RD({controlled_buffer_1_out_2, controlled_buffer_1_out}));
  port_C PC (
    .D0_D7(\Упр_слово ), .Pc0_Pc3_in_WR(Pc0_Pc7[3:0]), .Pc0_Pc3_out_RD(Pc0_Pc7[3:0]),
    .Pc4_Pc7_in_WR(Pc0_Pc7[7:4]), .Pc4_Pc7_out_RD(Pc0_Pc7[7:4]), .Enable(decoder_1_out2), .RESET(RESET),
    .CLK(clock_1_out), .Pc0_Pc3_out_WR(PC_pc0_pc3_out_wr[3:0]), .Pc0_Pc3_in_RD(controlled_buffer_1_out),
    .Pc4_Pc7_out_WR(PC_pc0_pc3_out_wr[7:4]), .Pc4_Pc7_in_RD(controlled_buffer_1_out_2));
  port_B PB (
    .D0_D7(\Упр_слово ), .PB_in_WR(Pb0_Pb7), .PB_out_RD(Pb0_Pb7), .Enable(decoder_1_out1), .RESET(RESET),
    .CLK(clock_1_out), .PB_out_WR(PB_pb_out_wr),
    .PA_in_RD({controlled_buffer_1_out_2, controlled_buffer_1_out}));
endmodule

module port_A (
  input  [7:0] D0_D7,
  input  [7:0] PA_in_WR,
  input  [7:0] PA_in_RD,
  input  Enable,
  input  RESET,
  input  CLK,
  output [7:0] PA_out_WR,
  output [7:0] PA_out_RD
);

  wire not_1_out;
  wire [7:0] controlled_buffer_2_out, PA_q;

  Register PA (.D(PA_in_WR), .en(Enable), .Q(PA_q), .clk(CLK), .clr(RESET));
  Register PA_2 (.D(controlled_buffer_2_out), .en(Enable), .Q(PA_out_RD), .clk(CLK), .clr(RESET));
  assign PA_out_WR = not_1_out ? PA_q : 8'bz;  // Controlled_Buffer controlled_buffer_1
  not not_1 (not_1_out, D0_D7[4]);
  assign controlled_buffer_2_out = D0_D7[4] ? PA_in_RD : 8'bz;  // Controlled_Buffer controlled_buffer_2
endmodule

module port_B (
  input  [7:0] D0_D7,
  input  [7:0] PB_in_WR,
  input  [7:0] PA_in_RD,
  input  Enable,
  input  RESET,
  input  CLK,
  output [7:0] PB_out_WR,
  output [7:0] PB_out_RD
);

  wire not_1_out;
  wire [7:0] controlled_buffer_2_out, PB_q;

  Register PB (.D(PB_in_WR), .en(Enable), .Q(PB_q), .clk(CLK), .clr(RESET));
  Register PB_2 (.D(controlled_buffer_2_out), .en(Enable), .Q(PB_out_RD), .clk(CLK), .clr(RESET));
  assign PB_out_WR = not_1_out ? PB_q : 8'bz;  // Controlled_Buffer controlled_buffer_1
  not not_1 (not_1_out, D0_D7[1]);
  assign controlled_buffer_2_out = D0_D7[1] ? PA_in_RD : 8'bz;  // Controlled_Buffer controlled_buffer_2
endmodule

module port_C (
  input  [7:0] D0_D7,
  input  [3:0] Pc0_Pc3_in_WR,
  input  [3:0] Pc0_Pc3_in_RD,
  input  [3:0] Pc4_Pc7_in_WR,
  input  [3:0] Pc4_Pc7_in_RD,
  input  Enable,
  input  RESET,
  input  CLK,
  output [3:0] Pc0_Pc3_out_WR,
  output [3:0] Pc0_Pc3_out_RD,
  output [3:0] Pc4_Pc7_out_WR,
  output [3:0] Pc4_Pc7_out_RD
);

  wire not_1_out, not_2_out;
  wire [3:0] controlled_buffer_2_out, controlled_buffer_4_out, Pc0_Pc3_q, Pc4_Pc7_q;

  Register #(.width(4)) Pc0_Pc3 (.D(Pc0_Pc3_in_WR), .en(Enable), .Q(Pc0_Pc3_q), .clk(CLK), .clr(RESET));
  Register #(.width(4)) Pc0_Pc3_2 (
    .D(controlled_buffer_2_out), .en(Enable), .Q(Pc0_Pc3_out_RD), .clk(CLK), .clr(RESET));
  Register #(.width(4)) Pc4_Pc7 (.D(Pc4_Pc7_in_WR), .en(Enable), .Q(Pc4_Pc7_q), .clk(CLK), .clr(RESET));
  Register #(.width(4)) Pc4_Pc7_2 (
    .D(controlled_buffer_4_out), .en(Enable), .Q(Pc4_Pc7_out_RD), .clk(CLK), .clr(RESET));
  assign Pc0_Pc3_out_WR = not_1_out ? Pc0_Pc3_q : 4'bz;  // Controlled_Buffer controlled_buffer_1
  not not_1 (not_1_out, D0_D7[0]);
  assign controlled_buffer_2_out = D0_D7[0] ? Pc0_Pc3_in_RD : 4'bz;  // Controlled_Buffer controlled_buffer_2
  assign Pc4_Pc7_out_WR = not_2_out ? Pc4_Pc7_q : 4'bz;  // Controlled_Buffer controlled_buffer_3
  not not_2 (not_2_out, D0_D7[3]);
  assign controlled_buffer_4_out = D0_D7[3] ? Pc4_Pc7_in_RD : 4'bz;  // Controlled_Buffer controlled_buffer_4
endmodule
